# Fritzing sketch ButtonRead (saved by Fritzing 0.9.3b)
breadboards: 1

parts:
  Part3 = Arduino Uno (Rev3)
  S1 = Pushbutton [package="[SMD]"]
  J3 = Basic Servo
  J4 = female pin header, 3 pins [form="♀ (female)"]

nets:
  5V: Part3.A0, Part3.5V, S1.Pin_1, S1.Pin_2, S1.Pin_3, S1.Pin_4, J3.vcc, J4.pin2
  N1: Part3.D10_PWM/SS, J3.pulse, J4.pin1
  GND: Part3.GND, J3.gnd, J4.pin3
