# Fritzing sketch LDR_LED (saved by Fritzing 0.9.3b)
breadboards: 1

parts:
  Part4 = Arduino Uno (Rev3)
  R2 = Photocell (LDR) [package=THT]
  LED1 = LED - 5mm [color="Red (633nm)" package="5 mm [THT]"]
  R3 = Resistor [tolerance=±5% resistance=220 package=THT]

nets:
  N1: Part4.A0, R2.pin_1
  N2: Part4.D3_PWM, LED1.anode
  N3: Part4.GND, R2.pin_0, R3.Pin_1
  N4: LED1.cathode, R3.Pin_0
