# Fritzing sketch PWMPinLED (saved by Fritzing 0.9.3b)
breadboards: 1

parts:
  Part2 = Arduino Uno (Rev3)
  LED2 = LED - 5mm [color="Red (633nm)" package="5 mm [THT]"]

nets:
  N1: Part2.D10_PWM/SS, LED2.anode
  N2: Part2.GND, LED2.cathode
