# Fritzing sketch PotServo (saved by Fritzing 0.9.3b)
breadboards: 1

parts:
  Part4 = Arduino Uno (Rev3)
  R1 = Rotary Potentiometer (Small) [maximum_resistance=100kΩ package=THT]
  J6 = female pin header, 3 pins [form="♀ (female)"]
  J5 = Basic Servo

nets:
  N1: Part4.A0, R1.wiper
  N2: Part4.D10_PWM/SS, J6.pin1, J5.pulse
  GND: Part4.GND, R1.leg1, J6.pin3, J5.gnd
  5V: Part4.5V, R1.leg2, J6.pin2, J5.vcc
