# Fritzing sketch ServoWithPot (saved by Fritzing 0.9.3b)
breadboards: 1

parts:
  R1 = Rotary Potentiometer (Small) [maximum_resistance=100kΩ package=THT]
  R2 = Resistor [tolerance=±5% resistance=220 package=THT]
  R3 = Resistor [tolerance=±5% resistance=220 package=THT]
  Part3 = Arduino Uno (Rev3)
  J4 = female pin header, 3 pins [form="♀ (female)"]
  J3 = Basic Servo

nets:
  N1: R1.leg1, R2.Pin_0
  N2: R1.wiper, R3.Pin_0
  5V: R1.leg2, Part3.5V, J4.pin2, J3.vcc
  GND: R2.Pin_1, Part3.GND, J4.pin3, J3.gnd
  N3: R3.Pin_1, Part3.A0
  N4: Part3.D10_PWM/SS, J4.pin1, J3.pulse
